// Digital circuit rj32.dig as structural Verilog
module rj32 (
  input  clock,
  input  step,
  input  run,
  input  [15:0] D_prog,
  input  [15:0] D_in,
  output [15:0] R0,
  output [15:0] R1,
  output [15:0] R2,
  output [15:0] R3,
  output [7:0] PC,
  output halt,
  output error,
  output T,
  output rd_valid,
  output rs_valid,
  output [4:0] op,
  output sys,
  output stall,
  output [15:0] L,
  output [15:0] R,
  output [1:0] rd,
  output [1:0] rs,
  output jump,
  output [7:0] A_prog,
  output clock_m,
  output [13:0] A_data,
  output [15:0] D_out,
  output w_en
);

  wire control_1_p5, control_1_p6, control_1_p12, control_1_p13, decoder_1_p2, decoder_1_p3, en;
  wire [15:0] decoder_1_p1, execute_1_p4, fetch_1_instr_o, memaccess_1_wrval;

  not not_1 (clock_m, clock);
  fetch fetch_1 (
    .instr_i(D_prog), .clock(clock), .en(control_1_p13), .jump(jump), .value(R), .pc(A_prog),
    .instr_o(fetch_1_instr_o));
  // decoder decoder_1: pin names not known; wires that end beside it: decoder_1_p1, decoder_1_p2, decoder_1_p3, fetch_1_instr_o, rs, rd, L, R, sys, op, rs_valid, rd_valid
  // clockctrl clockctrl_1: pin names not known; wires that end beside it: clock, step, run, stall
  // control control_1: pin names not known; wires that end beside it: sys, op, stall, clock, control_1_p5, control_1_p6, T, halt, error, en, decoder_1_p3, control_1_p12, control_1_p13, jump
  // execute execute_1: pin names not known; wires that end beside it: L, R, control_1_p6, execute_1_p4, control_1_p5
  memaccess memaccess_1 (
    .result(execute_1_p4), .rdval(decoder_1_p1), .mem(decoder_1_p3), .store(control_1_p12), .D(D_in),
    .en(en), .wrval(memaccess_1_wrval), .A(A_data), .str(w_en), .D_in(D_out));
  // regfile regfile_1: pin names not known; wires that end beside it: rs, rd, memaccess_1_wrval, clock, en, decoder_1_p1, decoder_1_p2, R0, R1, R2, R3

  assign PC = A_prog;

  // Other names for the same wires on the sheet: A_data_t[13:0] = A_data; C = clock; D_in_t[15:0] = D_in;
  //   D_out_t[15:0] = D_out; D_prog_t[15:0] = D_prog; error_t = error; halt_t = halt; jump_t = jump; L_t[15:0] = L;
  //   op_t[4:0] = op; A_prog_t[7:0] = A_prog; PC_t[7:0] = A_prog; R_t[15:0] = R; rd_t[1:0] = rd; rdvalid_t = rd_valid;
  //   rs_t[1:0] = rs; rsvalid_t = rs_valid; stall_t = stall; sys_t = sys; T_t = T; W_en_t = w_en

  // Notes on the sheet:
  //   clock: Hz: 10
  //   rj45 Creates
endmodule
